# Fritzing sketch lazserial3 (saved by Fritzing 0.9.2b)
breadboards: 1

parts:
  Parte1 = Arduino Uno (Rev3)
  S1 = Pushbutton [package="[SMD]"]
  S2 = Pushbutton [package="[THT]"]
  LED1 = LED - 3mm [color="Blue (525nm)" package="3 mm [THT]"]
  LED2 = LED - 3mm [color="Red (633nm)" package="3 mm [THT]"]
  R1 = Resistor [tolerance=±5% resistance=470 package="0402 [SMD]"]
  R2 = Resistor [tolerance=±5% resistance=470 package="0402 [SMD]"]
  Parte2 = Humidity Temperature Sensor SHT15

nets:
  N1: Parte1.D8, R1.Pin_1
  N2: Parte1.D9_PWM, R2.Pin_1
  GND: Parte1.GND, LED1.cathode, LED2.cathode, Parte2.GND
  N3: Parte1.D2, S1.Pin_3, S1.Pin_4
  N4: Parte1.D3_PWM, S2.Pin_3, S2.Pin_4
  5V: Parte1.5V, S1.Pin_1, S1.Pin_2, S2.Pin_1, S2.Pin_2, Parte2.VCC
  N5: LED1.anode, R2.Pin_0
  N6: LED2.anode, R1.Pin_0
